# Fritzing sketch prototype (saved by Fritzing 0.9.3b)
breadboards: 1

parts:
  Part2 = Adafruit Feather HUZZAH ESP8266 [part_number="Adafruit #2821"]
  Part3 = Adafruit OLED FeatherWing [part_number="Adafruit #2900"]
  Part4 = Adafruit TSL2561 [part_number="Adafruit #439"]
  Part1 = Lithium Ion Battery Pack 3.7V 4400mAh [part_number=354]

nets:
  N1: Part2.CH_PD, Part3.G
  N2: Part2.TXD, Part3.TX
  N3: Part2.RXD, Part3.RX
  N4: Part2.GPIO12/MISO, Part3.MISO, Part3.M
  N5: Part2.GPIO13/MOSI, Part3.MOSI, Part3.L
  N6: Part2.GPIO14/SCK, Part3.SCK, Part3.N
  N7: Part2.ADC, Part3.A
  GND: Part2.GND, Part3.GND, Part4.GND, Part1.negative
  3.3V: Part2.3.3V, Part3.3.3V, Part4.VIN
  N8: Part2.RESET, Part3.!RESET
  N9: Part2.VBAT, Part3.VBAT, Part1.positive
  N10: Part2.EN, Part3.EN
  N11: Part2.VBUS, Part3.USB
  N12: Part2.GPIO15, Part3.K
  N13: Part2.GPIO0, Part3.J
  N14: Part2.GPIO16, Part3.I
  N15: Part2.GPIO2, Part3.H
  N16: Part2.GPIO5/SCL, Part3.SCL, Part4.SCL
  N17: Part2.GPIO4/SDA, Part3.SDA, Part4.SDA

custom parts:
  Adafruit Feather HUZZAH ESP8266: his is the Adafruit Feather HUZZAH ESP8266 - our take on an 'all-in-one' ESP8266 WiFi development board with built in USB and battery charging. Its an ESP8266 WiFi module with all the extras you need, ready to rock! We have other boards in the Feather family, check'em out here. At the Feather HUZZAH's heart is an ESP8266 WiFi microcontroller clocked at 80 MHz and at 3.3V logic. This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
  Adafruit OLED FeatherWing: This is the FeatherWing OLED: it adds a 128x32 monochrome OLED plus 3 user buttons to any Feather main board. These displays are small, only about 1" diagonal, but very readable due to the high contrast of an OLED display. This screen is made of 128x32 individual white OLED pixels and because the display makes its own light, no backlight is required. This reduces the power required to run the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
  Adafruit TSL2561: The TSL2561 luminosity sensor is an advanced digital light sensor, ideal for use in a wide range of light situations. Compared to low cost CdS cells, this sensor is more precise, allowing for exact lux calculations and can be configured for different gain/timing ranges to detect light ranges from up to 0.1 - 40,000+ Lux on the fly. The best part of this sensor is that it contains both infrared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
  Lithium Ion Battery Pack 3.7V 4400mAh: This lithium ion pack is made of 2 balanced 2200mAh cells for a total of 4400mA capacity! The cells are connected in parallel and spot-welded to a protection circuit that provides over-voltage, under-voltage and over-current protection. Each cell can provide 1A of current for about 4 hours so all together the peak current you can draw is a little over 1.5 Amps. Note that these batteries are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
